# Fritzing sketch Sketch (saved by Fritzing 0.9.4)
breadboards: 1

parts:
  Componente1 = Arduino Mega 2560 (Rev3)
  Componente2 = RFID-RC522-v2
  J1 = Piezo Speaker
  LED1 = LED - 5mm [color="Red (633nm)" package="5 mm [THT]"]
  LED2 = LED - 5mm [color="Green (560nm)" package="5 mm [THT]"]
  R1 = Resistor [tolerance=±5% resistance=1k package="1206 [SMD]"]
  R2 = Resistor [tolerance=±5% resistance=1k package="1206 [SMD]"]

nets:
  GND: Componente1.GND, Componente2.GND, J1.pin1, LED1.cathode, LED2.cathode
  N1: Componente1.D9_PWM, R1.Pin_0
  N2: Componente1.D8_PWM, R2.Pin_0
  3V3: Componente1.3V3, Componente2.3.3V
  N3: Componente1.D5_PWM, Componente2.RST
  N4: Componente1.D7_PWM, J1.pin2
  N5: Componente1.D50, Componente2.MISO
  N6: Componente1.D51, Componente2.MOSI
  N7: Componente1.D52, Componente2.SCK
  N8: Componente1.D53, Componente2.SDA
  N9: LED1.anode, R2.Pin_1
  N10: LED2.anode, R1.Pin_1

notes:
  La comunicazione tra Arduino (master) e il modulo di lettura RFID (slave) avviene tramite il protocollo standard SPI (Serial Peripheral Interface).
  I cavi:
  Breadboard:
  Nero: ground
  Verde: 5V led verde
  Giallo: 5V led rosso
  Arancio: 5V led buzzer
  Modulo RFID RC522:
  Arancio: alimentazione 3.3V
  Grigio: segnale di reset
  Nero: ground
  Blu: MISO (Master Input Slave Output, slave -> master)
  Verde: MOSI (Master Output Slave Input, master -> slave)
  Bianco: SCK (Serial Clock, master -> slave)
  Viola: SDA/SS (Chip Select)
  Il pin non utilizzato del modulo RFID è il pin IRQ di Interrupt

custom parts:
  RFID-RC522-v2: A simple China made RFID-RC522 Reader; do check the pin labels, as this is a MFRC522 based clone.
